// Logisim project and-test.circ as structural Verilog: 1 circuit, main circuit main
module main (
  input  A,
  input  B,
  output Y1,
  output Y2,
  output Y3,
  output Y4
);

  nand nand_1 (Y1, A, B);
  nand nand_2 (Y2, A, B);
  nand nand_3 (Y3, A, B);
  nand nand_4 (Y4, A, B);
endmodule
