// Logisim project xor-test.circ as structural Verilog: 1 circuit, main circuit main
module main (
  input  A,
  input  B,
  output Y1,
  output Y2,
  output Y3,
  output Y4
);

  xor xor_1 (Y1, A, B);
  xor xor_2 (Y2, A, B);
  xor xor_3 (Y3, A, B);
  xor xor_4 (Y4, A, B);
endmodule
