# Fritzing sketch led-button (saved by Fritzing 0.9.3b)
breadboards: 1

parts:
  R1 = Resistor [tolerance=±5% resistance=330 package=THT]
  S1 = Pushbutton [package="[THT]"]
  LED1 = LED - 5mm [color="Red (633nm)" package="5 mm [THT]"]
  YwRobot_Power_Supply1 = YwRobot Breadboard Power Supply [part_number=545043]

nets:
  N1: R1.Pin_0, S1.Pin_1, S1.Pin_2
  N2: R1.Pin_1, YwRobot_Power_Supply1.GND#11, YwRobot_Power_Supply1.GND#12
  N3: S1.Pin_3, S1.Pin_4, LED1.cathode
  N4: LED1.anode, YwRobot_Power_Supply1.VCC#9, YwRobot_Power_Supply1.VCC#10
  N5: YwRobot_Power_Supply1.VCC#5, YwRobot_Power_Supply1.VCC#6
  N6: YwRobot_Power_Supply1.GND#13, YwRobot_Power_Supply1.GND#14

custom parts:
  YwRobot Breadboard Power Supply: The YwRobot Breadboard Power Supply (MB-V2) has two power rails; they can be 5V or 3V3. Power to the module can be provided through the female USB socket or through the A10 (female) 2.1mm power jack.
