# Fritzing sketch led (saved by Fritzing 0.9.3b)
breadboards: 1

parts:
  LED1 = LED - 5mm [color="Red (633nm)" package="5 mm [THT]"]
  YwRobot_Power_Supply1 = YwRobot Breadboard Power Supply [part_number=545043]
  R1 = Resistor [tolerance=±1% resistance=330 package=THT]

nets:
  N1: LED1.cathode, R1.Pin_0
  N2: LED1.anode, YwRobot_Power_Supply1.VCC#9, YwRobot_Power_Supply1.VCC#10
  N3: YwRobot_Power_Supply1.VCC#5, YwRobot_Power_Supply1.VCC#6
  N4: YwRobot_Power_Supply1.GND#11, YwRobot_Power_Supply1.GND#12, R1.Pin_1
  N5: YwRobot_Power_Supply1.GND#13, YwRobot_Power_Supply1.GND#14

custom parts:
  YwRobot Breadboard Power Supply: The YwRobot Breadboard Power Supply (MB-V2) has two power rails; they can be 5V or 3V3. Power to the module can be provided through the female USB socket or through the A10 (female) 2.1mm power jack.
