# Fritzing sketch nand-test (saved by Fritzing 0.9.3b)
breadboards: 1

parts:
  Part1 = Adafruit Micro USB Breakout [part_number="Adafruit #1833"]
  A = Pushbutton [package="[THT]"]
  B = Pushbutton [package="[THT]"]
  R1 = Resistor [tolerance=±5% resistance=1k package=THT]
  R2 = Resistor [tolerance=±5% resistance=1k package=THT]
  Y1 = LED - 5mm [color="Red (633nm)" package="5 mm [THT]"]
  Y2 = LED - 5mm [color="Red (633nm)" package="5 mm [THT]"]
  Y4 = LED - 5mm [color="Red (633nm)" package="5 mm [THT]"]
  Y3 = LED - 5mm [color="Red (633nm)" package="5 mm [THT]"]
  IC1 = 7400 [package="DIP (Dual Inline) [THT]"]

nets:
  GND: Part1.GND, R1.Pin_1, R2.Pin_1, Y1.cathode, Y2.cathode, Y4.cathode, Y3.cathode, IC1.GND
  N1: Part1.VBUS, A.Pin_3, A.Pin_4, B.Pin_3, B.Pin_4, IC1.VCC
  N2: A.Pin_1, A.Pin_2, R1.Pin_0, IC1.1A, IC1.2A, IC1.3A, IC1.4A
  N3: B.Pin_1, B.Pin_2, R2.Pin_0, IC1.1B, IC1.2B, IC1.3B, IC1.4B
  N4: Y1.anode, IC1.1Y
  N5: Y2.anode, IC1.2Y
  N6: Y4.anode, IC1.4Y
  N7: Y3.anode, IC1.3Y

custom parts:
  Adafruit Micro USB Breakout: Simple but effective - this breakout board has a USB Micro-B connector, with all 5 pins broken out. Great for pairing with a microcontroller with USB support, or adding USB 5V power to a project. We use a micro-AB connector with through-hole shielding pads for an excellent strong connection - it won't rip off by accident! Comes with one fully assembled and tested micro B breakout PCB and a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
  7400: Quad 2-input NAND gate
