# Fritzing sketch adder-1bit-full (saved by Fritzing 0.9.3b)
breadboards: 1

parts:
  IC1 = 7486 [package="DIP (Dual Inline) [THT]"]
  IC2 = 7432 [package="DIP (Dual Inline) [THT]"]
  IC3 = 7408 [package="DIP (Dual Inline) [THT]"]
  S0 = LED - 5mm [color="Red (633nm)" package="5 mm [THT]"]
  C1 = LED - 5mm [color="Red (633nm)" package="5 mm [THT]"]
  SW2 = DIP Switch 4 Position [package=dipswitch-04]
  SW3 = DIP Switch 4 Position [package=dipswitch-04]
  R1 = Resistor [tolerance=±5% resistance=1k package=THT]
  R3 = Resistor [tolerance=±5% resistance=1k package=THT]

nets:
  N1: IC1.1A, IC3.1A, SW2.1, R3.Pin_1
  N2: IC1.1B, IC3.1B, SW3.1, R1.Pin_1
  N3: IC1.1Y, IC1.2A, IC3.2A
  GND: IC1.2B, IC1.GND, IC2.GND, IC3.2B, IC3.GND, S0.cathode, C1.cathode, SW2.8, SW3.8
  N4: IC1.2Y, S0.anode
  VCC: IC1.VCC, IC2.VCC, IC3.VCC, R1.Pin_0, R3.Pin_0
  N5: IC2.2A, IC3.1Y
  N6: IC2.2B, IC3.2Y
  N7: IC2.2Y, C1.anode

notes:
  Full Adder 1-bit
  C0

custom parts:
  7486: Quad 2-input XOR gate
  7432: Quad 2-input OR gate
  7408: Quad 2-input AND gate
