# Fritzing sketch adder-1bit-half (saved by Fritzing 0.9.3b)
breadboards: 1

parts:
  IC1 = 7486 [package="DIP (Dual Inline) [THT]"]
  IC3 = 7408 [package="DIP (Dual Inline) [THT]"]
  S0 = LED - 5mm [color="Red (633nm)" package="5 mm [THT]"]
  C1 = LED - 5mm [color="Red (633nm)" package="5 mm [THT]"]
  SW2 = DIP Switch 4 Position [package=dipswitch-04]
  SW3 = DIP Switch 4 Position [package=dipswitch-04]
  R1 = Resistor [tolerance=±5% resistance=1k package=THT]
  R3 = Resistor [tolerance=±5% resistance=1k package=THT]

nets:
  N1: IC1.1A, IC3.1A, SW2.1, R3.Pin_1
  N2: IC1.1B, IC3.1B, SW3.1, R1.Pin_1
  N3: IC1.1Y, S0.anode
  GND: IC1.GND, IC3.GND, S0.cathode, C1.cathode, SW2.8, SW3.8
  VCC: IC1.VCC, IC3.VCC, R1.Pin_0, R3.Pin_0
  N4: IC3.1Y, C1.anode

notes:
  Half Adder

custom parts:
  7486: Quad 2-input XOR gate
  7408: Quad 2-input AND gate
