# Fritzing sketch adder-2bit (saved by Fritzing 0.9.3b)
breadboards: 1

parts:
  IC1 = 7486 [package="DIP (Dual Inline) [THT]"]
  IC2 = 7432 [package="DIP (Dual Inline) [THT]"]
  IC3 = 7408 [package="DIP (Dual Inline) [THT]"]
  S0 = LED - 5mm [color="Red (633nm)" package="5 mm [THT]"]
  C2 = LED - 5mm [color="Red (633nm)" package="5 mm [THT]"]
  SW2 = DIP Switch 4 Position [package=dipswitch-04]
  SW3 = DIP Switch 4 Position [package=dipswitch-04]
  R1 = Resistor [tolerance=±5% resistance=1k package=THT]
  R3 = Resistor [tolerance=±5% resistance=1k package=THT]
  R4 = Resistor [tolerance=±5% resistance=1k package=THT]
  R5 = Resistor [tolerance=±5% resistance=1k package=THT]
  S1 = LED - 5mm [color="Red (633nm)" package="5 mm [THT]"]

nets:
  N1: IC1.1A, IC3.1A, SW2.1, R3.Pin_1
  N2: IC1.1B, IC3.1B, SW3.1, R1.Pin_1
  N3: IC1.1Y, IC1.2A, IC3.2A
  GND: IC1.2B, IC1.GND, IC2.GND, IC3.2B, IC3.GND, S0.cathode, C2.cathode, SW2.7, SW2.8, SW3.7, SW3.8, S1.cathode
  N4: IC1.2Y, S0.anode
  N5: IC1.3Y, IC1.4B, IC3.4B
  N6: IC1.3B, IC3.3B, SW2.2, R5.Pin_1
  N7: IC1.3A, IC3.3A, SW3.2, R4.Pin_1
  N8: IC1.4Y, S1.anode
  N9: IC1.4A, IC2.2Y, IC3.4A
  VCC: IC1.VCC, IC2.VCC, IC3.VCC, R1.Pin_0, R3.Pin_0, R4.Pin_0, R5.Pin_0
  N10: IC2.2A, IC3.1Y
  N11: IC2.2B, IC3.2Y
  N12: IC2.3Y, C2.anode
  N13: IC2.3B, IC3.3Y
  N14: IC2.3A, IC3.4Y

notes:
  Adder 2-bit
  C0

custom parts:
  7486: Quad 2-input XOR gate
  7432: Quad 2-input OR gate
  7408: Quad 2-input AND gate
