# Fritzing sketch adder-4bit (saved by Fritzing 0.9.3b)
breadboards: 2

parts:
  IC1 = 7486 [package="DIP (Dual Inline) [THT]"]
  IC2 = 7432 [package="DIP (Dual Inline) [THT]"]
  IC3 = 7408 [package="DIP (Dual Inline) [THT]"]
  S2 = LED - 5mm [color="Red (633nm)" package="5 mm [THT]"]
  C4 = LED - 5mm [color="Red (633nm)" package="5 mm [THT]"]
  SW2 = DIP Switch 4 Position [package=dipswitch-04]
  SW3 = DIP Switch 4 Position [package=dipswitch-04]
  R1 = Resistor [tolerance=±5% resistance=1k package=THT]
  R3 = Resistor [tolerance=±5% resistance=1k package=THT]
  R4 = Resistor [tolerance=±5% resistance=1k package=THT]
  R5 = Resistor [tolerance=±5% resistance=1k package=THT]
  S3 = LED - 5mm [color="Red (633nm)" package="5 mm [THT]"]
  R6 = Resistor [tolerance=±5% resistance=1k package=THT]
  R7 = Resistor [tolerance=±5% resistance=1k package=THT]
  R8 = Resistor [tolerance=±5% resistance=1k package=THT]
  R9 = Resistor [tolerance=±5% resistance=1k package=THT]
  IC4 = 7486 [package="DIP (Dual Inline) [THT]"]
  IC5 = 7432 [package="DIP (Dual Inline) [THT]"]
  IC6 = 7408 [package="DIP (Dual Inline) [THT]"]
  S0 = LED - 5mm [color="Red (633nm)" package="5 mm [THT]"]
  S1 = LED - 5mm [color="Red (633nm)" package="5 mm [THT]"]
  SW4 = DIP Switch 4 Position [package=dipswitch-04]
  SW5 = DIP Switch 4 Position [package=dipswitch-04]

nets:
  N1: IC1.1A, IC3.1A, SW2.1, R3.Pin_1
  N2: IC1.1B, IC3.1B, SW3.1, R1.Pin_1
  N3: IC1.1Y, IC1.2A, IC3.2A
  N4: IC1.2B, IC3.2B, IC5.3Y
  N5: IC1.2Y, S2.anode
  GND: IC1.GND, IC2.GND, IC3.GND, S2.cathode, C4.cathode, SW2.7, SW2.8, SW3.7, SW3.8, S3.cathode, IC4.2B, IC4.GND, IC5.GND, IC6.2B, IC6.GND, S0.cathode, S1.cathode, SW4.7, SW4.8, SW5.7, SW5.8
  N6: IC1.3Y, IC1.4B, IC3.4B
  N7: IC1.3B, IC3.3B, SW2.2, R5.Pin_1
  N8: IC1.3A, IC3.3A, SW3.2, R4.Pin_1
  N9: IC1.4Y, S3.anode
  N10: IC1.4A, IC2.2Y, IC3.4A
  VCC: IC1.VCC, IC2.VCC, IC3.VCC, R1.Pin_0, R3.Pin_0, R4.Pin_0, R5.Pin_0, R6.Pin_0, R7.Pin_0, R8.Pin_0, R9.Pin_0, IC4.VCC, IC5.VCC, IC6.VCC
  N11: IC2.2A, IC3.1Y
  N12: IC2.2B, IC3.2Y
  N13: IC2.3Y, C4.anode
  N14: IC2.3B, IC3.3Y
  N15: IC2.3A, IC3.4Y
  N16: R6.Pin_1, IC4.1A, IC6.1A, SW5.1
  N17: R7.Pin_1, IC4.1B, IC6.1B, SW4.1
  N18: R8.Pin_1, IC4.3B, IC6.3B, SW5.2
  N19: R9.Pin_1, IC4.3A, IC6.3A, SW4.2
  N20: IC4.1Y, IC4.2A, IC6.2A
  N21: IC4.2Y, S0.anode
  N22: IC4.3Y, IC4.4B, IC6.4B
  N23: IC4.4Y, S1.anode
  N24: IC4.4A, IC5.2Y, IC6.4A
  N25: IC5.2A, IC6.1Y
  N26: IC5.2B, IC6.2Y
  N27: IC5.3B, IC6.3Y
  N28: IC5.3A, IC6.4Y

notes:
  Adder 4-bit
  C0
  C2

custom parts:
  7486: Quad 2-input XOR gate
  7432: Quad 2-input OR gate
  7408: Quad 2-input AND gate
