// Logisim project adder.circ as structural Verilog: 12 circuits, main circuit half-adder
module test (
  input  Cin,
  input  Cin_2,
  input  [3:0] A,
  input  [7:0] A_2,
  input  [3:0] B,
  input  [7:0] B_2,
  input  SUB,
  input  SUB_2,
  input  [3:0] A_3,
  input  [7:0] A_4,
  input  [3:0] B_3,
  input  [7:0] B_4,
  input  [3:0] A_5,
  input  SUB_3,
  input  [7:0] A_6,
  input  SUB_4,
  input  [3:0] B_5,
  input  [7:0] B_6,
  output [3:0] S,
  output [7:0] S_2,
  output Cout,
  output Cout_2,
  output [3:0] S_3,
  output [7:0] S_4,
  output C,
  output C_2,
  output [3:0] S_5,
  output [7:0] S_6,
  output C_3,
  output C_4
);

  Hex_Digit_Display hex_digit_display_1 (.value(A));  // open: dp
  Hex_Digit_Display hex_digit_display_2 (.value(B));  // open: dp
  Hex_Digit_Display hex_digit_display_3 (.value(A_3));  // open: dp
  Hex_Digit_Display hex_digit_display_4 (.value(B_3));  // open: dp
  Hex_Digit_Display hex_digit_display_5 (.value(A_5));  // open: dp
  Hex_Digit_Display hex_digit_display_6 (.value(B_5));  // open: dp
  _4bit_adder u_4bit_adder_1 (
    .A1(A[0]), .B1(B[0]), .A2(A[1]), .B2(B[1]), .A3(A[2]), .B3(B[2]), .A4(A[3]), .B4(B[3]), .S1(S[0]),
    .S2(S[1]), .S3(S[2]), .S4(S[3]), .C0(Cin_2), .C4(Cout));
  _4bit_addsub u_4bit_addsub_1 (
    .A1(A_3[0]), .B1(B_3[0]), .A2(A_3[1]), .B2(B_3[1]), .A3(A_3[2]), .B3(B_3[2]), .A4(A_3[3]), .B4(B_3[3]),
    .S1(S_3[0]), .S2(S_3[1]), .S3(S_3[2]), .S4(S_3[3]), .SUB(SUB_2), .C4(C));
  _4bit_addsub2 u_4bit_addsub2_1 (
    .SUB(SUB_3), .S1(S_5[0]), .S2(S_5[1]), .S3(S_5[2]), .S4(S_5[3]), .C(C_3), .A4(A_5[3]), .A3(A_5[2]),
    .A2(A_5[1]), .A1(A_5[0]), .B4(B_5[3]), .B3(B_5[2]), .B2(B_5[1]), .B1(B_5[0]));
  Hex_Digit_Display hex_digit_display_7 (.value(S));  // open: dp
  Hex_Digit_Display hex_digit_display_8 (.value(S_3));  // open: dp
  Hex_Digit_Display hex_digit_display_9 (.value(S_5));  // open: dp
  Hex_Digit_Display hex_digit_display_10 (.value(A_2[7:4]));  // open: dp
  Hex_Digit_Display hex_digit_display_11 (.value(B_2[7:4]));  // open: dp
  Hex_Digit_Display hex_digit_display_12 (.value(A_4[7:4]));  // open: dp
  Hex_Digit_Display hex_digit_display_13 (.value(B_4[7:4]));  // open: dp
  Hex_Digit_Display hex_digit_display_14 (.value(A_6[7:4]));  // open: dp
  Hex_Digit_Display hex_digit_display_15 (.value(B_6[7:4]));  // open: dp
  Hex_Digit_Display hex_digit_display_16 (.value(A_2[3:0]));  // open: dp
  Hex_Digit_Display hex_digit_display_17 (.value(B_2[3:0]));  // open: dp
  Hex_Digit_Display hex_digit_display_18 (.value(A_4[3:0]));  // open: dp
  Hex_Digit_Display hex_digit_display_19 (.value(B_4[3:0]));  // open: dp
  Hex_Digit_Display hex_digit_display_20 (.value(A_6[3:0]));  // open: dp
  Hex_Digit_Display hex_digit_display_21 (.value(B_6[3:0]));  // open: dp
  _8bit_adder u_8bit_adder_1 (
    .A1(A_2[0]), .B1(B_2[0]), .A2(A_2[1]), .B2(B_2[1]), .A3(A_2[2]), .B3(B_2[2]), .A4(A_2[3]), .B4(B_2[3]),
    .A5(A_2[4]), .B5(B_2[4]), .A6(A_2[5]), .B6(B_2[5]), .A7(A_2[6]), .B7(B_2[6]), .A8(A_2[7]), .B8(B_2[7]),
    .S1(S_2[0]), .S2(S_2[1]), .S3(S_2[2]), .S4(S_2[3]), .S5(S_2[4]), .S6(S_2[5]), .S7(S_2[6]), .S8(S_2[7]),
    .C0(Cin), .C8(Cout_2));
  _8bit_addsub u_8bit_addsub_1 (
    .A1(A_4[0]), .B1(B_4[0]), .A2(A_4[1]), .B2(B_4[1]), .A3(A_4[2]), .B3(B_4[2]), .A4(A_4[3]), .B4(B_4[3]),
    .A5(A_4[4]), .B5(B_4[4]), .A6(A_4[5]), .B6(B_4[5]), .A7(A_4[6]), .B7(B_4[6]), .A8(A_4[7]), .B8(B_4[7]),
    .S1(S_4[0]), .S2(S_4[1]), .S3(S_4[2]), .S4(S_4[3]), .S5(S_4[4]), .S6(S_4[5]), .S7(S_4[6]), .S8(S_4[7]),
    .SUB(SUB), .C4(C_2));
  Hex_Digit_Display hex_digit_display_22 (.value(S_2[7:4]));  // open: dp
  Hex_Digit_Display hex_digit_display_23 (.value(S_4[7:4]));  // open: dp
  _8bit_addsub2 u_8bit_addsub2_1 (
    .SUB(SUB_4), .S1(S_6[0]), .S2(S_6[1]), .S3(S_6[2]), .S4(S_6[3]), .S5(S_6[4]), .S6(S_6[5]), .S7(S_6[6]),
    .S8(S_6[7]), .C(C_4), .A8(A_6[7]), .A7(A_6[6]), .A6(A_6[5]), .A5(A_6[4]), .A4(A_6[3]), .A3(A_6[2]),
    .A2(A_6[1]), .A1(A_6[0]), .B8(B_6[7]), .B7(B_6[6]), .B6(B_6[5]), .B5(B_6[4]), .B4(B_6[3]), .B3(B_6[2]),
    .B2(B_6[1]), .B1(B_6[0]));
  Hex_Digit_Display hex_digit_display_24 (.value(S_2[3:0]));  // open: dp
  Hex_Digit_Display hex_digit_display_25 (.value(S_4[3:0]));  // open: dp
  Hex_Digit_Display hex_digit_display_26 (.value(S_6[7:4]));  // open: dp
  Hex_Digit_Display hex_digit_display_27 (.value(S_6[3:0]));  // open: dp

  // Notes on the sheet:
  //   4-bit adder
  //   4-bit adder/sub
  //   4-bit adder/sub
  //   8-bit adder
  //   8-bit adder/sub
  //   8-bit adder/sub
endmodule

module half_adder (
  input  A,
  input  B,
  output S,
  output C
);

  xor xor_1 (S, A, B);
  and and_1 (C, A, B);
endmodule

module full_adder (
  input  Cin,
  input  A,
  input  B,
  output S,
  output Cout
);

  wire and_1_out, and_2_out, xor_1_out;

  xor xor_1 (xor_1_out, A, B);
  and and_1 (and_1_out, A, B);
  xor xor_2 (S, Cin, xor_1_out);
  and and_2 (and_2_out, Cin, xor_1_out);
  or or_1 (Cout, and_2_out, and_1_out);
endmodule

module _4bit_adder (
  input  C0,
  input  A1,
  input  B1,
  input  A2,
  input  B2,
  input  A3,
  input  B3,
  input  A4,
  input  B4,
  output S1,
  output S2,
  output S3,
  output S4,
  output C4
);

  wire full_adder_1_cout, full_adder_2_cout, full_adder_3_cout;

  full_adder full_adder_1 (.A(A1), .B(B1), .S(S1), .Cout(full_adder_1_cout), .Cin(C0));
  full_adder full_adder_2 (.A(A2), .B(B2), .S(S2), .Cout(full_adder_2_cout), .Cin(full_adder_1_cout));
  full_adder full_adder_3 (.A(A3), .B(B3), .S(S3), .Cout(full_adder_3_cout), .Cin(full_adder_2_cout));
  full_adder full_adder_4 (.A(A4), .B(B4), .S(S4), .Cout(C4), .Cin(full_adder_3_cout));
endmodule

module _4bit_addsub (
  input  SUB,
  input  A1,
  input  B1,
  input  A2,
  input  B2,
  input  A3,
  input  B3,
  input  A4,
  input  B4,
  output S1,
  output S2,
  output S3,
  output S4,
  output C4
);

  wire full_adder_1_cout, full_adder_2_cout, full_adder_3_cout, xor_1_out, xor_2_out, xor_3_out, xor_4_out;

  full_adder full_adder_1 (.A(A1), .B(xor_1_out), .S(S1), .Cout(full_adder_1_cout), .Cin(SUB));
  xor xor_1 (xor_1_out, B1, SUB);
  full_adder full_adder_2 (.A(A2), .B(xor_2_out), .S(S2), .Cout(full_adder_2_cout), .Cin(full_adder_1_cout));
  xor xor_2 (xor_2_out, B2, SUB);
  full_adder full_adder_3 (.A(A3), .B(xor_3_out), .S(S3), .Cout(full_adder_3_cout), .Cin(full_adder_2_cout));
  xor xor_3 (xor_3_out, B3, SUB);
  full_adder full_adder_4 (.A(A4), .B(xor_4_out), .S(S4), .Cout(C4), .Cin(full_adder_3_cout));
  xor xor_4 (xor_4_out, B4, SUB);
endmodule

module _8bit_adder (
  input  C0,
  input  A1,
  input  B1,
  input  A2,
  input  B2,
  input  A3,
  input  B3,
  input  A4,
  input  B4,
  input  A5,
  input  B5,
  input  A6,
  input  B6,
  input  A7,
  input  B7,
  input  A8,
  input  B8,
  output S1,
  output S2,
  output S3,
  output S4,
  output S5,
  output S6,
  output S7,
  output S8,
  output C8
);

  wire full_adder_1_cout, full_adder_2_cout, full_adder_3_cout, full_adder_4_cout, full_adder_5_cout,
       full_adder_6_cout, full_adder_7_cout;

  full_adder full_adder_1 (.A(A1), .B(B1), .S(S1), .Cout(full_adder_1_cout), .Cin(C0));
  full_adder full_adder_2 (.A(A2), .B(B2), .S(S2), .Cout(full_adder_2_cout), .Cin(full_adder_1_cout));
  full_adder full_adder_3 (.A(A3), .B(B3), .S(S3), .Cout(full_adder_3_cout), .Cin(full_adder_2_cout));
  full_adder full_adder_4 (.A(A4), .B(B4), .S(S4), .Cout(full_adder_4_cout), .Cin(full_adder_3_cout));
  full_adder full_adder_5 (.A(A5), .B(B5), .S(S5), .Cout(full_adder_5_cout), .Cin(full_adder_4_cout));
  full_adder full_adder_6 (.A(A6), .B(B6), .S(S6), .Cout(full_adder_6_cout), .Cin(full_adder_5_cout));
  full_adder full_adder_7 (.A(A7), .B(B7), .S(S7), .Cout(full_adder_7_cout), .Cin(full_adder_6_cout));
  full_adder full_adder_8 (.A(A8), .B(B8), .S(S8), .Cout(C8), .Cin(full_adder_7_cout));
endmodule

module _8bit_addsub (
  input  SUB,
  input  A1,
  input  B1,
  input  A2,
  input  B2,
  input  A3,
  input  B3,
  input  A4,
  input  B4,
  input  A5,
  input  B5,
  input  A6,
  input  B6,
  input  A7,
  input  B7,
  input  A8,
  input  B8,
  output S1,
  output S2,
  output S3,
  output S4,
  output S5,
  output S6,
  output S7,
  output S8,
  output C4
);

  wire full_adder_1_cout, full_adder_2_cout, full_adder_3_cout, full_adder_4_cout, full_adder_5_cout,
       full_adder_6_cout, full_adder_7_cout, xor_1_out, xor_2_out, xor_3_out, xor_4_out, xor_5_out,
       xor_6_out, xor_7_out, xor_8_out;

  full_adder full_adder_1 (.A(A1), .B(xor_1_out), .S(S1), .Cout(full_adder_1_cout), .Cin(SUB));
  xor xor_1 (xor_1_out, B1, SUB);
  full_adder full_adder_2 (.A(A2), .B(xor_2_out), .S(S2), .Cout(full_adder_2_cout), .Cin(full_adder_1_cout));
  xor xor_2 (xor_2_out, B2, SUB);
  full_adder full_adder_3 (.A(A3), .B(xor_3_out), .S(S3), .Cout(full_adder_3_cout), .Cin(full_adder_2_cout));
  xor xor_3 (xor_3_out, B3, SUB);
  full_adder full_adder_4 (.A(A4), .B(xor_4_out), .S(S4), .Cout(full_adder_4_cout), .Cin(full_adder_3_cout));
  xor xor_4 (xor_4_out, B4, SUB);
  full_adder full_adder_5 (.A(A5), .B(xor_5_out), .S(S5), .Cout(full_adder_5_cout), .Cin(full_adder_4_cout));
  xor xor_5 (xor_5_out, B5, SUB);
  full_adder full_adder_6 (.A(A6), .B(xor_6_out), .S(S6), .Cout(full_adder_6_cout), .Cin(full_adder_5_cout));
  xor xor_6 (xor_6_out, B6, SUB);
  full_adder full_adder_7 (.A(A7), .B(xor_7_out), .S(S7), .Cout(full_adder_7_cout), .Cin(full_adder_6_cout));
  xor xor_7 (xor_7_out, B7, SUB);
  full_adder full_adder_8 (.A(A8), .B(xor_8_out), .S(S8), .Cout(C4), .Cin(full_adder_7_cout));
  xor xor_8 (xor_8_out, B8, SUB);
endmodule

module _4bit_addsub2 (
  input  A4,
  input  A3,
  input  A2,
  input  A1,
  input  SUB,
  input  B4,
  input  B3,
  input  B2,
  input  B1,
  output S1,
  output S2,
  output S3,
  output S4,
  output C
);

  wire xor_1_out, xor_2_out, xor_3_out, xor_4_out;

  xor xor_1 (xor_1_out, SUB, B3);
  xor xor_2 (xor_2_out, SUB, B4);
  xor xor_3 (xor_3_out, SUB, B1);
  xor xor_4 (xor_4_out, SUB, B2);
  _4bit_adder u_4bit_adder_1 (
    .A1(A1), .B1(xor_3_out), .A2(A2), .B2(xor_4_out), .A3(A3), .B3(xor_1_out), .A4(A4), .B4(xor_2_out),
    .S1(S1), .S2(S2), .S3(S3), .S4(S4), .C0(SUB), .C4(C));
endmodule

module _8bit_addsub2 (
  input  SUB,
  input  A8,
  input  A7,
  input  A6,
  input  A5,
  input  A4,
  input  A3,
  input  A2,
  input  A1,
  input  B8,
  input  B7,
  input  B6,
  input  B5,
  input  B4,
  input  B3,
  input  B2,
  input  B1,
  output S1,
  output S2,
  output S3,
  output S4,
  output S5,
  output S6,
  output S7,
  output S8,
  output C
);

  wire n4bit_adder_2_c4, xor_1_out, xor_2_out, xor_3_out, xor_4_out, xor_5_out, xor_6_out, xor_7_out,
       xor_8_out;

  xor xor_1 (xor_1_out, SUB, B7);
  xor xor_2 (xor_2_out, SUB, B8);
  xor xor_3 (xor_3_out, SUB, B6);
  xor xor_4 (xor_4_out, SUB, B5);
  _4bit_adder u_4bit_adder_1 (
    .A1(A5), .B1(xor_4_out), .A2(A6), .B2(xor_3_out), .A3(A7), .B3(xor_1_out), .A4(A8), .B4(xor_2_out),
    .S1(S5), .S2(S6), .S3(S7), .S4(S8), .C0(n4bit_adder_2_c4), .C4(C));
  xor xor_5 (xor_5_out, SUB, B4);
  xor xor_6 (xor_6_out, SUB, B3);
  xor xor_7 (xor_7_out, SUB, B2);
  _4bit_adder u_4bit_adder_2 (
    .A1(A1), .B1(xor_8_out), .A2(A2), .B2(xor_7_out), .A3(A3), .B3(xor_6_out), .A4(A4), .B4(xor_5_out),
    .S1(S1), .S2(S2), .S3(S3), .S4(S4), .C0(SUB), .C4(n4bit_adder_2_c4));
  xor xor_8 (xor_8_out, SUB, B1);
endmodule

module adder_2bit (
  input  C0,
  input  A1,
  input  B1,
  input  A2,
  input  B2,
  output S1,
  output S2,
  output C2
);

  wire full_adder_1_cout;

  full_adder full_adder_1 (.A(A1), .B(B1), .S(S1), .Cout(full_adder_1_cout), .Cin(C0));
  full_adder full_adder_2 (.A(A2), .B(B2), .S(S2), .Cout(C2), .Cin(full_adder_1_cout));
endmodule

module adder_4bit (
  input  C0,
  input  A1,
  input  B1,
  input  A2,
  input  B2,
  input  A3,
  input  B3,
  input  A4,
  input  B4,
  output S1,
  output S2,
  output S3,
  output S4,
  output C4
);

  wire full_adder_1_cout, full_adder_2_cout, full_adder_3_cout;

  full_adder full_adder_1 (.A(A1), .B(B1), .S(S1), .Cout(full_adder_1_cout), .Cin(C0));
  full_adder full_adder_2 (.A(A2), .B(B2), .S(S2), .Cout(full_adder_2_cout), .Cin(full_adder_1_cout));
  full_adder full_adder_3 (.A(A3), .B(B3), .S(S3), .Cout(full_adder_3_cout), .Cin(full_adder_2_cout));
  full_adder full_adder_4 (.A(A4), .B(B4), .S(S4), .Cout(C4), .Cin(full_adder_3_cout));
endmodule

module test2 (
  input  C0,
  input  [3:0] A,
  input  [3:0] B,
  output [3:0] S,
  output C4
);

  Hex_Digit_Display hex_digit_display_1 (.value(A));  // open: dp
  Hex_Digit_Display hex_digit_display_2 (.value(B));  // open: dp
  adder_4bit adder_4bit_1 (
    .A1(A[0]), .B1(B[0]), .A2(A[1]), .B2(B[1]), .A3(A[2]), .B3(B[2]), .A4(A[3]), .B4(B[3]), .S1(S[0]),
    .S2(S[1]), .S3(S[2]), .S4(S[3]), .C0(C0), .C4(C4));
  Hex_Digit_Display hex_digit_display_3 (.value(S));  // open: dp

  // Notes on the sheet:
  //   4-bit adder
endmodule
