// Logisim project alu.circ as structural Verilog: 10 circuits, main circuit full-adder
module full_adder (
  input  Cin,
  input  A,
  input  B,
  output S,
  output Cout
);

  wire and_1_out, and_2_out, xor_1_out;

  xor xor_1 (xor_1_out, A, B);
  and and_1 (and_1_out, A, B);
  xor xor_2 (S, Cin, xor_1_out);
  and and_2 (and_2_out, Cin, xor_1_out);
  or or_1 (Cout, and_2_out, and_1_out);
endmodule

module adder_2bit (
  input  C0,
  input  A0,
  input  B0,
  input  A1,
  input  B1,
  output S0,
  output S1,
  output C2
);

  wire full_adder_1_cout;

  full_adder full_adder_1 (.A(A0), .B(B0), .S(S0), .Cout(full_adder_1_cout), .Cin(C0));
  full_adder full_adder_2 (.A(A1), .B(B1), .S(S1), .Cout(C2), .Cin(full_adder_1_cout));
endmodule

module adder_4bit (
  input  C0,
  input  A0,
  input  B0,
  input  A1,
  input  B1,
  input  A2,
  input  B2,
  input  A3,
  input  B3,
  output S0,
  output S1,
  output S2,
  output S3,
  output C4
);

  wire full_adder_1_cout, full_adder_2_cout, full_adder_3_cout;

  full_adder full_adder_1 (.A(A0), .B(B0), .S(S0), .Cout(full_adder_1_cout), .Cin(C0));
  full_adder full_adder_2 (.A(A1), .B(B1), .S(S1), .Cout(full_adder_2_cout), .Cin(full_adder_1_cout));
  full_adder full_adder_3 (.A(A2), .B(B2), .S(S2), .Cout(full_adder_3_cout), .Cin(full_adder_2_cout));
  full_adder full_adder_4 (.A(A3), .B(B3), .S(S3), .Cout(C4), .Cin(full_adder_3_cout));
endmodule

module adder_4bit_test (
  input  C0,
  input  [3:0] A,
  input  [3:0] B,
  output [3:0] S,
  output C4
);

  Hex_Digit_Display hex_digit_display_1 (.value(A));  // open: dp
  Hex_Digit_Display hex_digit_display_2 (.value(B));  // open: dp
  adder_4bit adder_4bit_1 (
    .A0(A[0]), .B0(B[0]), .A1(A[1]), .B1(B[1]), .A2(A[2]), .B2(B[2]), .A3(A[3]), .B3(B[3]), .S0(S[0]),
    .S1(S[1]), .S2(S[2]), .S3(S[3]), .C0(C0), .C4(C4));
  Hex_Digit_Display hex_digit_display_3 (.value(S));  // open: dp
endmodule

module addsub_4bit (
  input  SUB,
  input  A0,
  input  A1,
  input  A2,
  input  A3,
  input  B0,
  input  B1,
  input  B2,
  input  B3,
  output S0,
  output S1,
  output S2,
  output S3,
  output C4
);

  wire xor_1_out, xor_2_out, xor_3_out, xor_4_out;

  xor xor_1 (xor_1_out, SUB, B0);
  xor xor_2 (xor_2_out, SUB, B1);
  xor xor_3 (xor_3_out, SUB, B2);
  xor xor_4 (xor_4_out, SUB, B3);
  adder_4bit adder_4bit_1 (
    .A0(A0), .B0(xor_1_out), .A1(A1), .B1(xor_2_out), .A2(A2), .B2(xor_3_out), .A3(A3), .B3(xor_4_out),
    .S0(S0), .S1(S1), .S2(S2), .S3(S3), .C0(SUB), .C4(C4));
endmodule

module addsub_4bit_test (
  input  SUB,
  input  [3:0] A,
  input  [3:0] B,
  output [3:0] S,
  output C4
);

  Hex_Digit_Display hex_digit_display_1 (.value(A));  // open: dp
  Hex_Digit_Display hex_digit_display_2 (.value(B));  // open: dp
  addsub_4bit addsub_4bit_1 (
    .A0(A[0]), .A1(A[1]), .A2(A[2]), .A3(A[3]), .B0(B[0]), .B1(B[1]), .B2(B[2]), .B3(B[3]), .S0(S[0]),
    .S1(S[1]), .S2(S[2]), .S3(S[3]), .SUB(SUB), .C4(C4));
  Hex_Digit_Display hex_digit_display_3 (.value(S));  // open: dp
endmodule

module addsub_8bit (
  input  SUB,
  input  A0,
  input  A1,
  input  A2,
  input  A3,
  input  A4,
  input  A5,
  input  A6,
  input  A7,
  input  B0,
  input  B1,
  input  B2,
  input  B3,
  input  B4,
  input  B5,
  input  B6,
  input  B7,
  output S0,
  output S1,
  output S2,
  output S3,
  output S4,
  output S5,
  output S6,
  output S7,
  output C8
);

  wire adder_4bit_1_c4, xor_1_out, xor_2_out, xor_3_out, xor_4_out, xor_5_out, xor_6_out, xor_7_out,
       xor_8_out;

  xor xor_1 (xor_1_out, SUB, B0);
  xor xor_2 (xor_2_out, SUB, B1);
  xor xor_3 (xor_3_out, SUB, B2);
  xor xor_4 (xor_4_out, SUB, B3);
  xor xor_5 (xor_5_out, SUB, B4);
  xor xor_6 (xor_6_out, SUB, B5);
  xor xor_7 (xor_7_out, SUB, B6);
  xor xor_8 (xor_8_out, SUB, B7);
  adder_4bit adder_4bit_1 (
    .A0(A0), .B0(xor_1_out), .A1(A1), .B1(xor_2_out), .A2(A2), .B2(xor_3_out), .A3(A3), .B3(xor_4_out),
    .S0(S0), .S1(S1), .S2(S2), .S3(S3), .C0(SUB), .C4(adder_4bit_1_c4));
  adder_4bit adder_4bit_2 (
    .A0(A4), .B0(xor_5_out), .A1(A5), .B1(xor_6_out), .A2(A6), .B2(xor_7_out), .A3(A7), .B3(xor_8_out),
    .S0(S4), .S1(S5), .S2(S6), .S3(S7), .C0(adder_4bit_1_c4), .C4(C8));
endmodule

module addsub_8bit_test (
  input  SUB,
  input  [7:0] A,
  input  [7:0] B,
  output [7:0] S,
  output C8
);

  Hex_Digit_Display hex_digit_display_1 (.value(A[7:4]));  // open: dp
  Hex_Digit_Display hex_digit_display_2 (.value(A[3:0]));  // open: dp
  Hex_Digit_Display hex_digit_display_3 (.value(B[3:0]));  // open: dp
  Hex_Digit_Display hex_digit_display_4 (.value(B[7:4]));  // open: dp
  addsub_8bit addsub_8bit_1 (
    .A0(A[0]), .A1(A[1]), .A2(A[2]), .A3(A[3]), .A4(A[4]), .A5(A[5]), .A6(A[6]), .A7(A[7]), .B0(B[0]),
    .B1(B[1]), .B2(B[2]), .B3(B[3]), .B4(B[4]), .B5(B[5]), .B6(B[6]), .B7(B[7]), .S0(S[0]), .S1(S[1]),
    .S2(S[2]), .S3(S[3]), .S4(S[4]), .S5(S[5]), .S6(S[6]), .S7(S[7]), .SUB(SUB), .C8(C8));
  Hex_Digit_Display hex_digit_display_5 (.value(S[7:4]));  // open: dp
  Hex_Digit_Display hex_digit_display_6 (.value(S[3:0]));  // open: dp
endmodule

module mul_4bit (
  input  A0,
  input  A1,
  input  A2,
  input  A3,
  input  B0,
  input  B1,
  input  B2,
  input  B3,
  output C0,
  output C1,
  output C2,
  output C3,
  output C4,
  output C5,
  output C6,
  output C7
);

  wire adder_4bit_2_c4, adder_4bit_2_s1, adder_4bit_2_s2, adder_4bit_2_s3, adder_4bit_3_c4, adder_4bit_3_s1,
       adder_4bit_3_s2, adder_4bit_3_s3, and_1_out, and_2_out, and_3_out, and_4_out, and_5_out, and_6_out,
       and_7_out, and_8_out, and_9_out, and_10_out, and_11_out, and_12_out, and_13_out, and_14_out,
       and_15_out;

  and and_1 (and_1_out, A3, B3);
  and and_2 (and_2_out, A3, B2);
  and and_3 (and_3_out, A3, B0);
  and and_4 (and_4_out, A3, B1);
  and and_5 (and_5_out, A2, B3);
  and and_6 (and_6_out, A2, B2);
  adder_4bit adder_4bit_1 (
    .A0(adder_4bit_2_s1), .B0(and_3_out), .A1(adder_4bit_2_s2), .B1(and_4_out), .A2(adder_4bit_2_s3),
    .B2(and_2_out), .A3(adder_4bit_2_c4), .B3(and_1_out), .S0(C3), .S1(C4), .S2(C5), .S3(C6), .C0(1'b0),
    .C4(C7));
  and and_7 (and_7_out, A2, B1);
  and and_8 (and_8_out, A2, B0);
  and and_9 (and_9_out, A1, B3);
  and and_10 (and_10_out, A1, B2);
  adder_4bit adder_4bit_2 (
    .A0(adder_4bit_3_s1), .B0(and_8_out), .A1(adder_4bit_3_s2), .B1(and_7_out), .A2(adder_4bit_3_s3),
    .B2(and_6_out), .A3(adder_4bit_3_c4), .B3(and_5_out), .S0(C2), .S1(adder_4bit_2_s1),
    .S2(adder_4bit_2_s2), .S3(adder_4bit_2_s3), .C0(1'b0), .C4(adder_4bit_2_c4));
  and and_11 (and_11_out, A1, B0);
  and and_12 (and_12_out, A1, B1);
  and and_13 (and_13_out, A0, B3);
  and and_14 (and_14_out, A0, B2);
  adder_4bit adder_4bit_3 (
    .A0(and_15_out), .B0(and_11_out), .A1(and_14_out), .B1(and_12_out), .A2(and_13_out), .B2(and_10_out),
    .A3(1'b0), .B3(and_9_out), .S0(C1), .S1(adder_4bit_3_s1), .S2(adder_4bit_3_s2), .S3(adder_4bit_3_s3),
    .C0(1'b0), .C4(adder_4bit_3_c4));
  and and_15 (and_15_out, A0, B1);
  and and_16 (C0, A0, B0);
endmodule

module mul_4bit_test (
  input  [3:0] A,
  input  [3:0] B,
  output [7:0] C
);

  Hex_Digit_Display hex_digit_display_1 (.value(A));  // open: dp
  Hex_Digit_Display hex_digit_display_2 (.value(B));  // open: dp
  Hex_Digit_Display hex_digit_display_3 (.value(C[7:4]));  // open: dp
  mul_4bit mul_4bit_1 (
    .A0(A[0]), .A1(A[1]), .A2(A[2]), .A3(A[3]), .B0(B[0]), .B1(B[1]), .B2(B[2]), .B3(B[3]), .C0(C[0]),
    .C1(C[1]), .C2(C[2]), .C3(C[3]), .C4(C[4]), .C5(C[5]), .C6(C[6]), .C7(C[7]));
  Hex_Digit_Display hex_digit_display_4 (.value(C[3:0]));  // open: dp
endmodule
