// Logisim project alu.tpl.circ as structural Verilog: 3 circuits, main circuit adder-4bit-test
module full_adder (
  input  Cin,
  input  A,
  input  B,
  output S,
  output Cout
);

  wire and_1_out, and_2_out, xor_1_out;

  xor xor_1 (xor_1_out, A, B);
  and and_1 (and_1_out, A, B);
  xor xor_2 (S, Cin, xor_1_out);
  and and_2 (and_2_out, Cin, xor_1_out);
  or or_1 (Cout, and_2_out, and_1_out);
endmodule

module adder_4bit (
  input  C0,
  input  A0,
  input  B0,
  input  A1,
  input  B1,
  input  A2,
  input  B2,
  input  A3,
  input  B3,
  output S0,
  output S1,
  output S2,
  output S3,
  output C4
);

  wire full_adder_1_cout, full_adder_2_cout, full_adder_3_cout;

  full_adder full_adder_1 (.A(A0), .B(B0), .S(S0), .Cout(full_adder_1_cout), .Cin(C0));
  full_adder full_adder_2 (.A(A1), .B(B1), .S(S1), .Cout(full_adder_2_cout), .Cin(full_adder_1_cout));
  full_adder full_adder_3 (.A(A2), .B(B2), .S(S2), .Cout(full_adder_3_cout), .Cin(full_adder_2_cout));
  full_adder full_adder_4 (.A(A3), .B(B3), .S(S3), .Cout(C4), .Cin(full_adder_3_cout));
endmodule

module adder_4bit_test (
  input  C0,
  input  [3:0] A,
  input  [3:0] B,
  output [3:0] S,
  output C4
);

  Hex_Digit_Display hex_digit_display_1 (.value(A));  // open: dp
  Hex_Digit_Display hex_digit_display_2 (.value(B));  // open: dp
  adder_4bit adder_4bit_1 (
    .A0(A[0]), .B0(B[0]), .A1(A[1]), .B1(B[1]), .A2(A[2]), .B2(B[2]), .A3(A[3]), .B3(B[3]), .S0(S[0]),
    .S1(S[1]), .S2(S[2]), .S3(S[3]), .C0(C0), .C4(C4));
  Hex_Digit_Display hex_digit_display_3 (.value(S));  // open: dp
endmodule
