# Fritzing sketch latch-d-nand (saved by Fritzing 0.9.3b)
breadboards: 1

parts:
  D = Pushbutton [package="[THT]"]
  R2 = Resistor [tolerance=±5% resistance=1k package=THT]
  En = Pushbutton [package="[THT]"]
  Q = LED - 5mm [color="Red (633nm)" package="5 mm [THT]"]
  Q' = LED - 5mm [color="Red (633nm)" package="5 mm [THT]"]
  R3 = Resistor [tolerance=±5% resistance=1k package=THT]
  IC1 = 7400 [package="DIP (Dual Inline) [THT]"]

nets:
  N1: D.Pin_1, D.Pin_2, En.Pin_3, En.Pin_4, IC1.VCC
  N2: D.Pin_3, D.Pin_4, R2.Pin_0, IC1.4A
  N3: R2.Pin_1, Q.cathode, Q'.cathode, R3.Pin_1, IC1.GND
  N4: En.Pin_1, En.Pin_2, R3.Pin_0, IC1.3B, IC1.4B
  N5: Q.anode, IC1.1Y, IC1.2A
  N6: Q'.anode, IC1.1B, IC1.2Y
  N7: IC1.1A, IC1.3A, IC1.4Y
  N8: IC1.2B, IC1.3Y

notes:
  D Latch

custom parts:
  7400: Quad 2-input NAND gate
