# Fritzing sketch latch-sr-en (saved by Fritzing 0.9.3b)
breadboards: 1

parts:
  IC1 = 7402 [package="DIP (Dual Inline) [THT]"]
  R = Pushbutton [package="[THT]"]
  S = Pushbutton [package="[THT]"]
  R1 = Resistor [tolerance=±5% resistance=1k package=THT]
  R2 = Resistor [tolerance=±5% resistance=1k package=THT]
  IC2 = 7408 [package="DIP (Dual Inline) [THT]"]
  EN = Pushbutton [package="[THT]"]
  R3 = Resistor [tolerance=±5% resistance=1k package=THT]
  Q = LED - 5mm [color="Red (633nm)" package="5 mm [THT]"]
  Q' = LED - 5mm [color="Red (633nm)" package="5 mm [THT]"]

nets:
  N1: IC1.1Y, IC1.2A, Q.anode
  N2: IC1.1A, IC2.1Y
  N3: IC1.1B, IC1.2Y, Q'.anode
  N4: IC1.2B, IC2.2Y
  GND: IC1.GND, R1.Pin_1, R2.Pin_1, IC2.GND, R3.Pin_1, Q.cathode, Q'.cathode
  VCC: IC1.VCC, R.Pin_1, R.Pin_2, S.Pin_1, S.Pin_2, IC2.VCC, EN.Pin_1, EN.Pin_2
  N5: R.Pin_3, R.Pin_4, R1.Pin_0, IC2.1A
  N6: S.Pin_3, S.Pin_4, R2.Pin_0, IC2.2B
  N7: IC2.1B, IC2.2A, EN.Pin_3, EN.Pin_4, R3.Pin_0

notes:
  SR Latch with Enable

custom parts:
  7402: Quad 2-input NOR gate
  7408: Quad 2-input AND gate
