# Fritzing sketch latch-sr (saved by Fritzing 0.9.3b)
breadboards: 1

parts:
  IC1 = 7402 [package="DIP (Dual Inline) [THT]"]
  R = Pushbutton [package="[THT]"]
  S = Pushbutton [package="[THT]"]
  R1 = Resistor [tolerance=±5% resistance=1k package=THT]
  R2 = Resistor [tolerance=±5% resistance=1k package=THT]
  Q = LED - 5mm [color="Red (633nm)" package="5 mm [THT]"]
  Q' = LED - 5mm [color="Red (633nm)" package="5 mm [THT]"]

nets:
  N1: IC1.1Y, IC1.2A, Q.anode
  N2: IC1.1A, R.Pin_1, R.Pin_2, R2.Pin_0
  N3: IC1.1B, IC1.2Y, Q'.anode
  N4: IC1.2B, S.Pin_3, S.Pin_4, R1.Pin_0
  N5: IC1.GND, R1.Pin_1, R2.Pin_1, Q.cathode, Q'.cathode
  N6: IC1.VCC, R.Pin_3, R.Pin_4, S.Pin_1, S.Pin_2

notes:
  SR Latch

custom parts:
  7402: Quad 2-input NOR gate
