// Logisim project latch.circ as structural Verilog
module sr_latch (
  input  R,
  input  S,
  output Q,
  output Q_prime
);

  nor nor_1 (Q, R, Q_prime);
  nor nor_2 (Q_prime, Q, S);
endmodule

module sr_latch_en (
  input  R,
  input  EN,
  input  S,
  output Q,
  output Q_prime
);

  wire and_1_out, and_2_out;

  and and_1 (and_1_out, R, EN);
  and and_2 (and_2_out, EN, S);
  nor nor_1 (Q, and_1_out, Q_prime);
  nor nor_2 (Q_prime, Q, and_2_out);
endmodule

module d_latch (
  input  EN,
  input  D,
  output Q,
  output Q_prime
);

  wire and_1_out, and_2_out, not_1_out;

  not not_1 (not_1_out, D);
  and and_1 (and_1_out, not_1_out, EN);
  and and_2 (and_2_out, EN, D);
  nor nor_1 (Q, and_1_out, Q_prime);
  nor nor_2 (Q_prime, Q, and_2_out);
endmodule

module d_latch__nand (
  input  D,
  input  EN,
  output Q,
  output Q_prime
);

  wire nand_1_out, nand_2_out;

  nand nand_1 (nand_1_out, D, EN);
  nand nand_2 (nand_2_out, nand_1_out, EN);
  nand nand_3 (Q, nand_1_out, Q_prime);
  nand nand_4 (Q_prime, Q, nand_2_out);
endmodule

module d_latch__nor (
  input  D,
  input  EN_prime,
  output Q,
  output Q_prime
);

  wire nor_1_out, nor_2_out;

  nor nor_1 (nor_1_out, D, EN_prime);
  nor nor_2 (nor_2_out, nor_1_out, EN_prime);
  nor nor_3 (Q, nor_1_out, Q_prime);
  nor nor_4 (Q_prime, Q, nor_2_out);
endmodule
