# Fritzing sketch clock (saved by Fritzing 0.9.3b)
breadboards: 1

parts:
  U1 = 555 Timer [package="DIP8 [THT]"]
  R3 = Resistor [tolerance=±5% resistance=1k package=THT]
  R4 = Resistor [tolerance=±5% resistance=10M package=THT]
  C1 = Ceramic Capacitor [capacitance=10nF package="100 mil [THT, multilayer]"]
  C2 = Tantalum Capacitor [capacitance=100nF package="100 mil [THT, tantalum]"]
  CLK = LED - 5mm [color="Yellow (585nm)" package="5 mm [THT]"]

nets:
  N1: U1.Pin_1, C2.-, CLK.cathode
  N2: U1.Pin_2, U1.Pin_6, R4.Pin_0, C2.+
  N3: U1.Pin_3, CLK.anode
  N4: U1.Pin_5, C1.1
  N5: U1.Pin_7, R3.Pin_1, R4.Pin_1
  N6: U1.Pin_8, R3.Pin_0

notes:
  Clock Generator (555 Astable Oscillator)
