# Fritzing sketch flipflop-jk (saved by Fritzing 0.9.3b)
breadboards: 1

parts:
  K = Pushbutton [package="[THT]"]
  R2 = Resistor [tolerance=±5% resistance=1k package=THT]
  Clk = Pushbutton [package="[THT]"]
  Q = LED - 5mm [color="Red (633nm)" package="5 mm [THT]"]
  Q' = LED - 5mm [color="Red (633nm)" package="5 mm [THT]"]
  R3 = Resistor [tolerance=±5% resistance=1k package=THT]
  IC1 = 7400 [package="DIP (Dual Inline) [THT]"]
  IC2 = 7402 [package="DIP (Dual Inline) [THT]"]
  IC3 = 7432 [package="DIP (Dual Inline) [THT]"]
  IC4 = 7408 [package="DIP (Dual Inline) [THT]"]
  J = Pushbutton [package="[THT]"]
  R4 = Resistor [tolerance=±5% resistance=1k package=THT]

nets:
  GND: K.Pin_1, K.Pin_2, R2.Pin_1, Q.cathode, Q'.cathode, IC1.GND, IC2.GND, IC3.GND, IC4.GND, R4.Pin_1
  N1: K.Pin_3, K.Pin_4, R3.Pin_1, IC4.3B
  N2: R2.Pin_0, Clk.Pin_1, Clk.Pin_2, IC1.3B, IC1.4B, IC2.3A, IC2.4A
  VCC: Clk.Pin_3, Clk.Pin_4, R3.Pin_0, IC1.VCC, IC2.VCC, IC3.VCC, IC4.VCC, J.Pin_1, J.Pin_2
  N3: Q.anode, IC1.1Y, IC1.2A, IC4.3A
  N4: Q'.anode, IC1.1B, IC1.2Y, IC4.4A
  N5: IC1.1A, IC1.3A, IC1.4Y
  N6: IC1.2B, IC1.3Y
  N7: IC1.4A, IC2.1Y, IC2.2A
  N8: IC2.1A, IC2.3B, IC2.4Y
  N9: IC2.1B, IC2.2Y
  N10: IC2.2B, IC2.3Y
  N11: IC2.4B, IC3.3Y
  N12: IC3.3B, IC4.3Y
  N13: IC3.3A, IC4.4Y
  N14: IC4.4B, J.Pin_3, J.Pin_4, R4.Pin_0

notes:
  JK Flip-Flop

custom parts:
  7400: Quad 2-input NAND gate
  7402: Quad 2-input NOR gate
  7432: Quad 2-input OR gate
  7408: Quad 2-input AND gate
