# Fritzing sketch flipflop-t (saved by Fritzing 0.9.3b)
breadboards: 1

parts:
  T = Pushbutton [package="[THT]"]
  R2 = Resistor [tolerance=±5% resistance=1k package=THT]
  Q = LED - 5mm [color="Red (633nm)" package="5 mm [THT]"]
  Q' = LED - 5mm [color="Red (633nm)" package="5 mm [THT]"]
  IC1 = 7400 [package="DIP (Dual Inline) [THT]"]
  IC2 = 7402 [package="DIP (Dual Inline) [THT]"]
  IC3 = 7486 [package="DIP (Dual Inline) [THT]"]

nets:
  VCC: T.Pin_1, T.Pin_2, IC1.VCC, IC2.VCC, IC3.VCC
  N1: T.Pin_3, T.Pin_4, R2.Pin_0, IC3.1B
  GND: R2.Pin_1, Q.cathode, Q'.cathode, IC1.GND, IC2.GND, IC3.GND
  N2: Q.anode, IC1.1Y, IC1.2A, IC3.1A
  N3: Q'.anode, IC1.1B, IC1.2Y
  N4: IC1.1A, IC1.3A, IC1.4Y
  N5: IC1.2B, IC1.3Y
  N6: IC1.3B, IC1.4B, IC2.3A, IC2.4A
  N7: IC1.4A, IC2.1Y, IC2.2A
  N8: IC2.1A, IC2.3B, IC2.4Y
  N9: IC2.2B, IC2.3Y
  N10: IC2.4B, IC3.1Y

notes:
  T Flip-Flop
  CLK

custom parts:
  7400: Quad 2-input NAND gate
  7402: Quad 2-input NOR gate
  7486: Quad 2-input XOR gate
