// Logisim project flipflop.circ as structural Verilog: 16 circuits, main circuit main
module main (
  input  in_1,
  input  in_2
);

  wire clock_1_out;
  wire [3:0] counter_4bit_1_a0;

  Clock clock_1 (.out(clock_1_out));
  counter_4bit counter_4bit_1 (
    .Clk(clock_1_out), .Clear_prime(in_2), .A0(counter_4bit_1_a0[0]), .A1(counter_4bit_1_a0[1]),
    .A2(counter_4bit_1_a0[2]), .A3(counter_4bit_1_a0[3]), .Count(in_1));
  Hex_Digit_Display hex_digit_display_1 (.value(counter_4bit_1_a0));  // open: dp
endmodule

module d_latch_nand (
  input  D,
  input  En,
  output Q,
  output Q_prime
);

  wire nand_1_out, nand_2_out;

  nand nand_1 (nand_1_out, D, En);
  nand nand_2 (nand_2_out, nand_1_out, En);
  nand nand_3 (Q, nand_1_out, Q_prime);
  nand nand_4 (Q_prime, Q, nand_2_out);
endmodule

module d_latch_nor (
  input  D,
  input  En_prime,
  output Q,
  output Q_prime
);

  wire nor_1_out, nor_2_out;

  nor nor_1 (nor_1_out, D, En_prime);
  nor nor_2 (nor_2_out, nor_1_out, En_prime);
  nor nor_3 (Q, nor_1_out, Q_prime);
  nor nor_4 (Q_prime, Q, nor_2_out);
endmodule

module d_flipflop_mslave_negedge (
  input  D,
  input  Clk,
  output Q,
  output Q_prime
);

  wire d_latch_nand_1_q;

  d_latch_nand d_latch_nand_1 (.D(D), .En(Clk), .Q(d_latch_nand_1_q));  // open: Q_prime
  d_latch_nor d_latch_nor_1 (.D(d_latch_nand_1_q), .En_prime(Clk), .Q(Q), .Q_prime(Q_prime));
endmodule

module d_flipflop_mslave_posedge (
  input  D,
  input  Clk,
  output Q,
  output Q_prime
);

  wire d_latch_nor_1_q;

  d_latch_nor d_latch_nor_1 (.D(D), .En_prime(Clk), .Q(d_latch_nor_1_q));  // open: Q_prime
  d_latch_nand d_latch_nand_1 (.D(d_latch_nor_1_q), .En(Clk), .Q(Q), .Q_prime(Q_prime));
endmodule

module d_flipflop_edgedetect (
  input  D,
  input  Clk,
  output Q,
  output Q_prime
);

  wire and_1_out, not_1_out, not_2_out, not_3_out;

  not not_1 (not_1_out, Clk);
  not not_2 (not_2_out, not_1_out);
  and and_1 (and_1_out, Clk, not_3_out);
  not not_3 (not_3_out, not_2_out);
  d_latch_nand d_latch_nand_1 (.D(D), .En(and_1_out), .Q(Q), .Q_prime(Q_prime));

  // Notes on the sheet:
  //   D Flip-Flop (with Positive Edge Detector)
endmodule

module d_flipflop (
  input  Clk,
  input  D,
  output Q,
  output Q_prime
);

  wire nand_1_out, nand_2_out, nand_3_out, nand_4_out;

  nand nand_1 (nand_1_out, nand_4_out, nand_2_out);
  nand nand_2 (nand_2_out, nand_1_out, Clk);
  nand nand_3 (nand_3_out, nand_2_out, Clk, nand_4_out);
  nand nand_4 (nand_4_out, nand_3_out, D);
  nand nand_5 (Q, nand_2_out, Q_prime);
  nand nand_6 (Q_prime, Q, nand_3_out);
endmodule

module jk_flipflop (
  input  J,
  input  K,
  input  Clk,
  output Q,
  output Q_prime
);

  wire and_1_out, and_2_out, not_1_out, or_1_out;

  and and_1 (and_1_out, Q_prime, J);
  not not_1 (not_1_out, K);
  and and_2 (and_2_out, not_1_out, Q);
  or or_1 (or_1_out, and_1_out, and_2_out);
  d_flipflop d_flipflop_1 (.Clk(Clk), .D(or_1_out), .Q(Q), .Q_prime(Q_prime));

  // Notes on the sheet:
  //   JK Flip-Flop
endmodule

module t_flipflop (
  input  T,
  input  Clk,
  output Q,
  output Q_prime
);

  wire xor_1_out;

  xor xor_1 (xor_1_out, T, Q);
  d_flipflop d_flipflop_1 (.Clk(Clk), .D(xor_1_out), .Q(Q), .Q_prime(Q_prime));

  // Notes on the sheet:
  //   T Flip-Flop
endmodule

module d_flipflop_rst (
  input  Clk,
  input  D,
  input  Rst_prime,
  output Q,
  output Q_prime
);

  wire nand_1_out, nand_2_out, nand_3_out, nand_4_out;

  nand nand_1 (nand_1_out, nand_4_out, nand_2_out);
  nand nand_2 (nand_2_out, nand_1_out, Clk, Rst_prime);
  nand nand_3 (nand_3_out, nand_2_out, Clk, nand_4_out);
  nand nand_4 (nand_4_out, nand_3_out, D, Rst_prime);
  nand nand_5 (Q, nand_2_out, Q_prime);
  nand nand_6 (Q_prime, Q, nand_3_out, Rst_prime);
endmodule

module jk_flipflop_rst (
  input  J,
  input  K,
  input  Clk,
  input  Rst_prime,
  output Q,
  output Q_prime
);

  wire and_1_out, and_2_out, not_1_out, or_1_out;

  and and_1 (and_1_out, Q_prime, J);
  not not_1 (not_1_out, K);
  and and_2 (and_2_out, not_1_out, Q);
  or or_1 (or_1_out, and_1_out, and_2_out);
  d_flipflop_rst d_flipflop_rst_1 (.Clk(Clk), .D(or_1_out), .Rst_prime(Rst_prime), .Q(Q), .Q_prime(Q_prime));
endmodule

module t_flipflop_rst (
  input  T,
  input  Clk,
  input  Rst_prime,
  output Q,
  output Q_prime
);

  wire xor_1_out;

  xor xor_1 (xor_1_out, T, Q);
  d_flipflop_rst d_flipflop_rst_1 (.Clk(Clk), .D(xor_1_out), .Rst_prime(Rst_prime), .Q(Q), .Q_prime(Q_prime));
endmodule

module counter_4bit_dff (
  input  Clk,
  input  Clear_prime,
  output A0,
  output A1,
  output A2,
  output A3
);

  wire d_flipflop_rst_1_q_prime, d_flipflop_rst_2_q_prime, d_flipflop_rst_3_q_prime, d_flipflop_rst_4_q_prime;

  d_flipflop_rst d_flipflop_rst_1 (
    .Clk(Clk), .D(d_flipflop_rst_1_q_prime), .Rst_prime(Clear_prime), .Q(A0),
    .Q_prime(d_flipflop_rst_1_q_prime));
  d_flipflop_rst d_flipflop_rst_2 (
    .Clk(d_flipflop_rst_1_q_prime), .D(d_flipflop_rst_2_q_prime), .Rst_prime(Clear_prime), .Q(A1),
    .Q_prime(d_flipflop_rst_2_q_prime));
  d_flipflop_rst d_flipflop_rst_3 (
    .Clk(d_flipflop_rst_2_q_prime), .D(d_flipflop_rst_3_q_prime), .Rst_prime(Clear_prime), .Q(A2),
    .Q_prime(d_flipflop_rst_3_q_prime));
  d_flipflop_rst d_flipflop_rst_4 (
    .Clk(d_flipflop_rst_3_q_prime), .D(d_flipflop_rst_4_q_prime), .Rst_prime(Clear_prime), .Q(A3),
    .Q_prime(d_flipflop_rst_4_q_prime));

  // Notes on the sheet:
  //   Counter 4-bit (D Flip-Flop)
endmodule

module counter_4bit (
  input  Count,
  input  Clk,
  input  Clear_prime,
  output A0,
  output A1,
  output A2,
  output A3
);

  wire t_flipflop_rst_1_q_prime, t_flipflop_rst_2_q_prime, t_flipflop_rst_3_q_prime;

  t_flipflop_rst t_flipflop_rst_1 (
    .T(Count), .Clk(Clk), .Q(A0), .Q_prime(t_flipflop_rst_1_q_prime), .Rst_prime(Clear_prime));
  t_flipflop_rst t_flipflop_rst_2 (
    .T(Count), .Clk(t_flipflop_rst_1_q_prime), .Q(A1), .Q_prime(t_flipflop_rst_2_q_prime),
    .Rst_prime(Clear_prime));
  t_flipflop_rst t_flipflop_rst_3 (
    .T(Count), .Clk(t_flipflop_rst_2_q_prime), .Q(A2), .Q_prime(t_flipflop_rst_3_q_prime),
    .Rst_prime(Clear_prime));
  t_flipflop_rst t_flipflop_rst_4 (
    .T(Count), .Clk(t_flipflop_rst_3_q_prime), .Q(A3), .Rst_prime(Clear_prime));  // open: Q_prime

  // Notes on the sheet:
  //   Counter 4-bit
endmodule

module counter_4bit_down (
  input  Count,
  input  Clk,
  input  Clear_prime,
  output A0,
  output A1,
  output A2,
  output A3
);

  t_flipflop_rst t_flipflop_rst_1 (.T(Count), .Clk(Clk), .Q(A0), .Rst_prime(Clear_prime));  // open: Q_prime
  t_flipflop_rst t_flipflop_rst_2 (.T(Count), .Clk(A0), .Q(A1), .Rst_prime(Clear_prime));  // open: Q_prime
  t_flipflop_rst t_flipflop_rst_3 (.T(Count), .Clk(A1), .Q(A2), .Rst_prime(Clear_prime));  // open: Q_prime
  t_flipflop_rst t_flipflop_rst_4 (.T(Count), .Clk(A2), .Q(A3), .Rst_prime(Clear_prime));  // open: Q_prime

  // Notes on the sheet:
  //   Counter 4-bit (Down)
endmodule

module counter_4bit_sync (
  input  Count,
  input  Clk,
  input  Clear_prime,
  output A0,
  output A1,
  output A2,
  output A3,
  output Next
);

  wire and_1_out, and_2_out, and_3_out;

  t_flipflop_rst t_flipflop_rst_1 (.T(Count), .Clk(Clk), .Q(A0), .Rst_prime(Clear_prime));  // open: Q_prime
  and and_1 (and_1_out, Count, A0);
  t_flipflop_rst t_flipflop_rst_2 (.T(and_1_out), .Clk(Clk), .Q(A1), .Rst_prime(Clear_prime));  // open: Q_prime
  and and_2 (and_2_out, and_1_out, A1);
  t_flipflop_rst t_flipflop_rst_3 (.T(and_2_out), .Clk(Clk), .Q(A2), .Rst_prime(Clear_prime));  // open: Q_prime
  and and_3 (and_3_out, and_2_out, A2);
  t_flipflop_rst t_flipflop_rst_4 (.T(and_3_out), .Clk(Clk), .Q(A3), .Rst_prime(Clear_prime));  // open: Q_prime
  and and_4 (Next, and_3_out, A3);

  // Notes on the sheet:
  //   Counter 4-bit (Synchronous)
endmodule
