# Fritzing sketch counter-2bit-noclk (saved by Fritzing 0.9.3b)
breadboards: 1

parts:
  A0 = LED - 5mm [color="Red (633nm)" package="5 mm [THT]"]
  IC1 = 7400 [package="DIP (Dual Inline) [THT]"]
  IC2 = 7402 [package="DIP (Dual Inline) [THT]"]
  IC7 = 7400 [package="DIP (Dual Inline) [THT]"]
  IC8 = 7402 [package="DIP (Dual Inline) [THT]"]
  A1 = LED - 5mm [color="Red (633nm)" package="5 mm [THT]"]

nets:
  GND: A0.cathode, IC1.GND, IC2.GND, IC7.GND, IC8.GND, A1.cathode
  N1: A0.anode, IC1.1Y, IC1.2A
  N2: IC1.1A, IC1.3A, IC1.4Y
  N3: IC1.1B, IC1.2Y, IC2.4B, IC7.3B, IC7.4B, IC8.3A, IC8.4A
  N4: IC1.2B, IC1.3Y
  N5: IC1.3B, IC1.4B, IC2.3A, IC2.4A
  N6: IC1.4A, IC2.1Y, IC2.2A
  VCC: IC1.VCC, IC2.VCC, IC7.VCC, IC8.VCC
  N7: IC2.1A, IC2.3B, IC2.4Y
  N8: IC2.2B, IC2.3Y
  N9: IC7.1A, IC7.3A, IC7.4Y
  N10: IC7.1B, IC7.2Y, IC8.4B
  N11: IC7.1Y, IC7.2A, A1.anode
  N12: IC7.2B, IC7.3Y
  N13: IC7.4A, IC8.1Y, IC8.2A
  N14: IC8.1A, IC8.3B, IC8.4Y
  N15: IC8.1B, IC8.2Y
  N16: IC8.2B, IC8.3Y

notes:
  Counter 2-Bit
  CLK

custom parts:
  7400: Quad 2-input NAND gate
  7402: Quad 2-input NOR gate
