# Fritzing sketch counter-2bit (saved by Fritzing 0.9.3b)
breadboards: 1

parts:
  A0 = LED - 5mm [color="Red (633nm)" package="5 mm [THT]"]
  IC1 = 7400 [package="DIP (Dual Inline) [THT]"]
  IC2 = 7402 [package="DIP (Dual Inline) [THT]"]
  U1 = 555 Timer [package="DIP8 [THT]"]
  R3 = Resistor [tolerance=±5% resistance=1k package=THT]
  R4 = Resistor [tolerance=±5% resistance=10M package=THT]
  C1 = Ceramic Capacitor [capacitance=10nF package="100 mil [THT, multilayer]"]
  C2 = Tantalum Capacitor [capacitance=100nF package="100 mil [THT, tantalum]"]
  CLK = LED - 5mm [color="Yellow (585nm)" package="5 mm [THT]"]
  IC7 = 7400 [package="DIP (Dual Inline) [THT]"]
  IC8 = 7402 [package="DIP (Dual Inline) [THT]"]
  A1 = LED - 5mm [color="Red (633nm)" package="5 mm [THT]"]

nets:
  GND: A0.cathode, IC1.GND, IC2.GND, U1.Pin_1, C2.-, CLK.cathode, IC7.GND, IC8.GND, A1.cathode
  N1: A0.anode, IC1.1Y, IC1.2A
  N2: IC1.1A, IC1.3A, IC1.4Y
  N3: IC1.1B, IC1.2Y, IC2.4B, IC7.3B, IC7.4B, IC8.3A, IC8.4A
  N4: IC1.2B, IC1.3Y
  N5: IC1.3B, IC1.4B, IC2.3A, IC2.4A, U1.Pin_3, CLK.anode
  N6: IC1.4A, IC2.1Y, IC2.2A
  VCC: IC1.VCC, IC2.VCC, U1.Pin_8, R3.Pin_0, IC7.VCC, IC8.VCC
  N7: IC2.1A, IC2.3B, IC2.4Y
  N8: IC2.2B, IC2.3Y
  N9: U1.Pin_2, U1.Pin_6, R4.Pin_0, C2.+
  N10: U1.Pin_5, C1.1
  N11: U1.Pin_7, R3.Pin_1, R4.Pin_1
  N12: IC7.1A, IC7.3A, IC7.4Y
  N13: IC7.1B, IC7.2Y, IC8.4B
  N14: IC7.1Y, IC7.2A, A1.anode
  N15: IC7.2B, IC7.3Y
  N16: IC7.4A, IC8.1Y, IC8.2A
  N17: IC8.1A, IC8.3B, IC8.4Y
  N18: IC8.1B, IC8.2Y
  N19: IC8.2B, IC8.3Y

notes:
  Counter 2-Bit

custom parts:
  7400: Quad 2-input NAND gate
  7402: Quad 2-input NOR gate
