# Fritzing sketch counter-4bit (saved by Fritzing 0.9.3b)
breadboards: 2

parts:
  A0 = LED - 5mm [color="Red (633nm)" package="5 mm [THT]"]
  IC1 = 7400 [package="DIP (Dual Inline) [THT]"]
  IC2 = 7402 [package="DIP (Dual Inline) [THT]"]
  U1 = 555 Timer [package="DIP8 [THT]"]
  R3 = Resistor [tolerance=±5% resistance=1k package=THT]
  R4 = Resistor [tolerance=±5% resistance=10M package=THT]
  C1 = Ceramic Capacitor [capacitance=10nF package="100 mil [THT, multilayer]"]
  C2 = Tantalum Capacitor [capacitance=100nF package="100 mil [THT, tantalum]"]
  CLK = LED - 5mm [color="Yellow (585nm)" package="5 mm [THT]"]
  IC7 = 7400 [package="DIP (Dual Inline) [THT]"]
  IC8 = 7402 [package="DIP (Dual Inline) [THT]"]
  A1 = LED - 5mm [color="Red (633nm)" package="5 mm [THT]"]
  A2 = LED - 5mm [color="Red (633nm)" package="5 mm [THT]"]
  IC9 = 7400 [package="DIP (Dual Inline) [THT]"]
  IC10 = 7402 [package="DIP (Dual Inline) [THT]"]
  IC11 = 7400 [package="DIP (Dual Inline) [THT]"]
  IC12 = 7402 [package="DIP (Dual Inline) [THT]"]
  A3 = LED - 5mm [color="Red (633nm)" package="5 mm [THT]"]

nets:
  GND: A0.cathode, IC1.GND, IC2.GND, U1.Pin_1, C2.-, CLK.cathode, IC7.GND, IC8.GND, A1.cathode, A2.cathode, IC9.GND, IC10.GND, IC11.GND, IC12.GND, A3.cathode
  N1: A0.anode, IC1.1Y, IC1.2A
  N2: IC1.1A, IC1.3A, IC1.4Y
  N3: IC1.1B, IC1.2Y, IC2.4B, IC7.3B, IC7.4B, IC8.3A, IC8.4A
  N4: IC1.2B, IC1.3Y
  N5: IC1.3B, IC1.4B, IC2.3A, IC2.4A, U1.Pin_3, CLK.anode
  N6: IC1.4A, IC2.1Y, IC2.2A
  VCC: IC1.VCC, IC2.VCC, U1.Pin_8, R3.Pin_0, IC7.VCC, IC8.VCC, IC9.VCC, IC10.VCC, IC11.VCC, IC12.VCC
  N7: IC2.1A, IC2.3B, IC2.4Y
  N8: IC2.2B, IC2.3Y
  N9: U1.Pin_2, U1.Pin_6, R4.Pin_0, C2.+
  N10: U1.Pin_5, C1.1
  N11: U1.Pin_7, R3.Pin_1, R4.Pin_1
  N12: IC7.1A, IC7.3A, IC7.4Y
  N13: IC7.1B, IC7.2Y, IC8.4B, IC9.3B, IC9.4B, IC10.3A, IC10.4A
  N14: IC7.1Y, IC7.2A, A1.anode
  N15: IC7.2B, IC7.3Y
  N16: IC7.4A, IC8.1Y, IC8.2A
  N17: IC8.1A, IC8.3B, IC8.4Y
  N18: IC8.1B, IC8.2Y
  N19: IC8.2B, IC8.3Y
  N20: A2.anode, IC9.1Y, IC9.2A
  N21: IC9.1A, IC9.3A, IC9.4Y
  N22: IC9.1B, IC9.2Y, IC10.4B, IC11.3B, IC11.4B, IC12.3A, IC12.4A
  N23: IC9.2B, IC9.3Y
  N24: IC9.4A, IC10.1Y, IC10.2A
  N25: IC10.1A, IC10.3B, IC10.4Y
  N26: IC10.2B, IC10.3Y
  N27: IC11.1A, IC11.3A, IC11.4Y
  N28: IC11.1B, IC11.2Y, IC12.4B
  N29: IC11.1Y, IC11.2A, A3.anode
  N30: IC11.2B, IC11.3Y
  N31: IC11.4A, IC12.1Y, IC12.2A
  N32: IC12.1A, IC12.3B, IC12.4Y
  N33: IC12.1B, IC12.2Y
  N34: IC12.2B, IC12.3Y

notes:
  Counter 4-Bit

custom parts:
  7400: Quad 2-input NAND gate
  7402: Quad 2-input NOR gate
