// Logisim project counter-fdiv.circ as structural Verilog
module d_flipflop (
  input  Clk,
  input  D,
  input  Rst_prime,
  output Q,
  output Q_prime
);

  wire nand_1_out, nand_2_out, nand_3_out, nand_4_out;

  nand nand_1 (nand_1_out, nand_4_out, nand_2_out);
  nand nand_2 (nand_2_out, nand_1_out, Clk, Rst_prime);
  nand nand_3 (nand_3_out, nand_2_out, Clk, nand_4_out);
  nand nand_4 (nand_4_out, nand_3_out, D, Rst_prime);
  nand nand_5 (Q, nand_2_out, Q_prime);
  nand nand_6 (Q_prime, Q, nand_3_out, Rst_prime);
endmodule

module counter_4bit_d (
  input  RST_prime,
  output f,
  output f_2,
  output f_4,
  output f_8,
  output f_16
);

  wire clock_1_out, d_flipflop_1_q_prime, d_flipflop_2_q_prime, d_flipflop_3_q_prime, d_flipflop_4_q_prime;

  not not_1 (f, clock_1_out);
  Clock clock_1 (.out(clock_1_out));
  d_flipflop d_flipflop_1 (
    .Clk(clock_1_out), .D(d_flipflop_1_q_prime), .Rst_prime(RST_prime), .Q(f_2),
    .Q_prime(d_flipflop_1_q_prime));
  d_flipflop d_flipflop_2 (
    .Clk(d_flipflop_1_q_prime), .D(d_flipflop_2_q_prime), .Rst_prime(RST_prime), .Q(f_4),
    .Q_prime(d_flipflop_2_q_prime));
  d_flipflop d_flipflop_3 (
    .Clk(d_flipflop_2_q_prime), .D(d_flipflop_3_q_prime), .Rst_prime(RST_prime), .Q(f_8),
    .Q_prime(d_flipflop_3_q_prime));
  d_flipflop d_flipflop_4 (
    .Clk(d_flipflop_3_q_prime), .D(d_flipflop_4_q_prime), .Rst_prime(RST_prime), .Q(f_16),
    .Q_prime(d_flipflop_4_q_prime));
endmodule
