// Logisim project counter.circ as structural Verilog
module d_flipflop (
  input  Clk,
  input  D,
  input  Rst_prime,
  output Q,
  output Q_prime
);

  wire nand_1_out, nand_2_out, nand_3_out, nand_4_out;

  nand nand_1 (nand_1_out, nand_4_out, nand_2_out);
  nand nand_2 (nand_2_out, nand_1_out, Clk, Rst_prime);
  nand nand_3 (nand_3_out, nand_2_out, Clk, nand_4_out);
  nand nand_4 (nand_4_out, nand_3_out, D, Rst_prime);
  nand nand_5 (Q, nand_2_out, Q_prime);
  nand nand_6 (Q_prime, Q, nand_3_out, Rst_prime);
endmodule

module jk_flipflop (
  input  J,
  input  K,
  input  Clk,
  input  Rst_prime,
  output Q,
  output Q_prime
);

  wire and_1_out, and_2_out, not_1_out, or_1_out;

  and and_1 (and_1_out, Q_prime, J);
  not not_1 (not_1_out, K);
  and and_2 (and_2_out, not_1_out, Q);
  or or_1 (or_1_out, and_1_out, and_2_out);
  d_flipflop d_flipflop_1 (.Clk(Clk), .D(or_1_out), .Rst_prime(Rst_prime), .Q(Q), .Q_prime(Q_prime));
endmodule

module t_flipflop (
  input  T,
  input  Clk,
  input  Rst_prime,
  output Q,
  output Q_prime
);

  wire xor_1_out;

  xor xor_1 (xor_1_out, Q, T);
  d_flipflop d_flipflop_1 (.Clk(Clk), .D(xor_1_out), .Rst_prime(Rst_prime), .Q(Q), .Q_prime(Q_prime));
endmodule

module counter_4bit_d (
  input  Clk,
  input  Clear_prime,
  output A0,
  output A1,
  output A2,
  output A3
);

  wire d_flipflop_1_q_prime, d_flipflop_2_q_prime, d_flipflop_3_q_prime, d_flipflop_4_q_prime;

  d_flipflop d_flipflop_1 (
    .Clk(Clk), .D(d_flipflop_1_q_prime), .Rst_prime(Clear_prime), .Q(A0), .Q_prime(d_flipflop_1_q_prime));
  d_flipflop d_flipflop_2 (
    .Clk(d_flipflop_1_q_prime), .D(d_flipflop_2_q_prime), .Rst_prime(Clear_prime), .Q(A1),
    .Q_prime(d_flipflop_2_q_prime));
  d_flipflop d_flipflop_3 (
    .Clk(d_flipflop_2_q_prime), .D(d_flipflop_3_q_prime), .Rst_prime(Clear_prime), .Q(A2),
    .Q_prime(d_flipflop_3_q_prime));
  d_flipflop d_flipflop_4 (
    .Clk(d_flipflop_3_q_prime), .D(d_flipflop_4_q_prime), .Rst_prime(Clear_prime), .Q(A3),
    .Q_prime(d_flipflop_4_q_prime));
endmodule

module counter_4bit_t (
  input  Count,
  input  Clk,
  input  Clear_prime,
  output A0,
  output A1,
  output A2,
  output A3
);

  wire t_flipflop_1_q_prime, t_flipflop_2_q_prime, t_flipflop_3_q_prime;

  t_flipflop t_flipflop_1 (.T(Count), .Clk(Clk), .Q(A0), .Q_prime(t_flipflop_1_q_prime), .Rst_prime(Clear_prime));
  t_flipflop t_flipflop_2 (
    .T(Count), .Clk(t_flipflop_1_q_prime), .Q(A1), .Q_prime(t_flipflop_2_q_prime), .Rst_prime(Clear_prime));
  t_flipflop t_flipflop_3 (
    .T(Count), .Clk(t_flipflop_2_q_prime), .Q(A2), .Q_prime(t_flipflop_3_q_prime), .Rst_prime(Clear_prime));
  t_flipflop t_flipflop_4 (.T(Count), .Clk(t_flipflop_3_q_prime), .Q(A3), .Rst_prime(Clear_prime));  // open: Q_prime
endmodule

module counter_4bit_t_down (
  input  Count,
  input  Clk,
  input  Clear_prime,
  output A0,
  output A1,
  output A2,
  output A3
);

  t_flipflop t_flipflop_1 (.T(Count), .Clk(Clk), .Q(A0), .Rst_prime(Clear_prime));  // open: Q_prime
  t_flipflop t_flipflop_2 (.T(Count), .Clk(A0), .Q(A1), .Rst_prime(Clear_prime));  // open: Q_prime
  t_flipflop t_flipflop_3 (.T(Count), .Clk(A1), .Q(A2), .Rst_prime(Clear_prime));  // open: Q_prime
  t_flipflop t_flipflop_4 (.T(Count), .Clk(A2), .Q(A3), .Rst_prime(Clear_prime));  // open: Q_prime
endmodule

module counter_4bit_t_sync (
  input  Count,
  input  Clk,
  input  Clear_prime,
  output Next,
  output A0,
  output A1,
  output A2,
  output A3
);

  wire and_1_out, and_2_out, and_3_out;

  and and_1 (and_1_out, Count, A0);
  t_flipflop t_flipflop_1 (.T(Count), .Clk(Clk), .Q(A0), .Rst_prime(Clear_prime));  // open: Q_prime
  t_flipflop t_flipflop_2 (.T(and_1_out), .Clk(Clk), .Q(A1), .Rst_prime(Clear_prime));  // open: Q_prime
  and and_2 (and_2_out, and_1_out, A1);
  and and_3 (and_3_out, and_2_out, A2);
  t_flipflop t_flipflop_3 (.T(and_2_out), .Clk(Clk), .Q(A2), .Rst_prime(Clear_prime));  // open: Q_prime
  t_flipflop t_flipflop_4 (.T(and_3_out), .Clk(Clk), .Q(A3), .Rst_prime(Clear_prime));  // open: Q_prime
  and and_4 (Next, and_3_out, A3);
endmodule

module counter_deca_jk (
  input  Count,
  input  Clk,
  input  Clear_prime,
  output Q1,
  output Q2,
  output Q4,
  output Q8
);

  wire and_1_out, jk_flipflop_1_q_prime, jk_flipflop_2_q_prime, jk_flipflop_4_q_prime;

  jk_flipflop jk_flipflop_1 (
    .J(Count), .K(Count), .Clk(Clk), .Rst_prime(Clear_prime), .Q(Q1), .Q_prime(jk_flipflop_1_q_prime));
  jk_flipflop jk_flipflop_2 (
    .J(jk_flipflop_4_q_prime), .K(Count), .Clk(jk_flipflop_1_q_prime), .Rst_prime(Clear_prime), .Q(Q2),
    .Q_prime(jk_flipflop_2_q_prime));
  and and_1 (and_1_out, Q2, Q4);
  jk_flipflop jk_flipflop_3 (
    .J(Count), .K(Count), .Clk(jk_flipflop_2_q_prime), .Rst_prime(Clear_prime), .Q(Q4));  // open: Q_prime
  jk_flipflop jk_flipflop_4 (
    .J(and_1_out), .K(Count), .Clk(jk_flipflop_1_q_prime), .Rst_prime(Clear_prime), .Q(Q8),
    .Q_prime(jk_flipflop_4_q_prime));
endmodule

module counter_deca_t (
  input  Count,
  input  Clk,
  input  Clear_prime,
  output Q1,
  output Q2,
  output Q4,
  output Q8
);

  wire _1010_out, and_1_out, t_flipflop_1_q_prime, t_flipflop_2_q_prime, t_flipflop_3_q_prime;

  and and_1 (and_1_out, Clear_prime, _1010_out);
  nand _1010 (_1010_out, ~Q1, Q2, ~Q4, Q8);  // NAND_Gate
  t_flipflop t_flipflop_1 (.T(Count), .Clk(Clk), .Q(Q1), .Q_prime(t_flipflop_1_q_prime), .Rst_prime(and_1_out));
  t_flipflop t_flipflop_2 (
    .T(Count), .Clk(t_flipflop_1_q_prime), .Q(Q2), .Q_prime(t_flipflop_2_q_prime), .Rst_prime(and_1_out));
  t_flipflop t_flipflop_3 (
    .T(Count), .Clk(t_flipflop_2_q_prime), .Q(Q4), .Q_prime(t_flipflop_3_q_prime), .Rst_prime(and_1_out));
  t_flipflop t_flipflop_4 (.T(Count), .Clk(t_flipflop_3_q_prime), .Q(Q8), .Rst_prime(and_1_out));  // open: Q_prime
endmodule

module counter_hexa_t (
  input  Count,
  input  Clk,
  input  Clear_prime,
  output Q1,
  output Q2,
  output Q4,
  output Q8
);

  wire _110_out, and_1_out, t_flipflop_1_q_prime, t_flipflop_2_q_prime;

  and and_1 (and_1_out, Clear_prime, _110_out);
  nand _110 (_110_out, ~Q1, Q2, Q4);  // NAND_Gate
  t_flipflop t_flipflop_1 (.T(Count), .Clk(Clk), .Q(Q1), .Q_prime(t_flipflop_1_q_prime), .Rst_prime(and_1_out));
  t_flipflop t_flipflop_2 (
    .T(Count), .Clk(t_flipflop_1_q_prime), .Q(Q2), .Q_prime(t_flipflop_2_q_prime), .Rst_prime(and_1_out));
  t_flipflop t_flipflop_3 (.T(Count), .Clk(t_flipflop_2_q_prime), .Q(Q4), .Rst_prime(and_1_out));  // open: Q_prime

  assign Q8 = 1'b0;
endmodule

module test_counter_8bit (
  input  Start,
  input  Reset_prime
);

  wire clock_1_out, not_1_out;
  wire [3:0] counter_4bit_t_1_a0, counter_4bit_t_2_a0;

  counter_4bit_t counter_4bit_t_1 (
    .Clk(not_1_out), .Clear_prime(Reset_prime), .A0(counter_4bit_t_1_a0[0]), .A1(counter_4bit_t_1_a0[1]),
    .A2(counter_4bit_t_1_a0[2]), .A3(counter_4bit_t_1_a0[3]), .Count(Start));
  not not_1 (not_1_out, counter_4bit_t_2_a0[3]);
  counter_4bit_t counter_4bit_t_2 (
    .Clk(clock_1_out), .Clear_prime(Reset_prime), .A0(counter_4bit_t_2_a0[0]), .A1(counter_4bit_t_2_a0[1]),
    .A2(counter_4bit_t_2_a0[2]), .A3(counter_4bit_t_2_a0[3]), .Count(Start));
  Clock clock_1 (.out(clock_1_out));
  Hex_Digit_Display hex_digit_display_1 (.value(counter_4bit_t_1_a0));  // open: dp
  Hex_Digit_Display hex_digit_display_2 (.value(counter_4bit_t_2_a0));  // open: dp
endmodule

module test_counter_3deca (
  input  Start,
  input  Reset_prime
);

  wire clock_1_out, not_1_out, not_2_out;
  wire [3:0] counter_deca_jk_1_q1, counter_deca_jk_2_q1, counter_deca_jk_3_q1;

  counter_deca_jk counter_deca_jk_1 (
    .Count(Start), .Clk(not_1_out), .Clear_prime(Reset_prime), .Q1(counter_deca_jk_1_q1[0]),
    .Q2(counter_deca_jk_1_q1[1]), .Q4(counter_deca_jk_1_q1[2]), .Q8(counter_deca_jk_1_q1[3]));
  not not_1 (not_1_out, counter_deca_jk_2_q1[3]);
  counter_deca_jk counter_deca_jk_2 (
    .Count(Start), .Clk(not_2_out), .Clear_prime(Reset_prime), .Q1(counter_deca_jk_2_q1[0]),
    .Q2(counter_deca_jk_2_q1[1]), .Q4(counter_deca_jk_2_q1[2]), .Q8(counter_deca_jk_2_q1[3]));
  not not_2 (not_2_out, counter_deca_jk_3_q1[3]);
  counter_deca_jk counter_deca_jk_3 (
    .Count(Start), .Clk(clock_1_out), .Clear_prime(Reset_prime), .Q1(counter_deca_jk_3_q1[0]),
    .Q2(counter_deca_jk_3_q1[1]), .Q4(counter_deca_jk_3_q1[2]), .Q8(counter_deca_jk_3_q1[3]));
  Clock clock_1 (.out(clock_1_out));
  Hex_Digit_Display hex_digit_display_1 (.value(counter_deca_jk_1_q1));  // open: dp
  Hex_Digit_Display hex_digit_display_2 (.value(counter_deca_jk_2_q1));  // open: dp
  Hex_Digit_Display hex_digit_display_3 (.value(counter_deca_jk_3_q1));  // open: dp
endmodule

module test_counter_60min (
  input  Start,
  input  Reset_prime
);

  wire clock_1_out, not_1_out, not_2_out, not_3_out;
  wire [3:0] counter_deca_t_1_q1, counter_deca_t_2_q1, counter_hexa_t_1_q1, counter_hexa_t_2_q1;

  counter_hexa_t counter_hexa_t_1 (
    .Count(Start), .Clk(not_1_out), .Clear_prime(Reset_prime), .Q1(counter_hexa_t_1_q1[0]),
    .Q2(counter_hexa_t_1_q1[1]), .Q4(counter_hexa_t_1_q1[2]), .Q8(counter_hexa_t_1_q1[3]));
  not not_1 (not_1_out, counter_deca_t_1_q1[3]);
  counter_deca_t counter_deca_t_1 (
    .Count(Start), .Clk(not_2_out), .Clear_prime(Reset_prime), .Q1(counter_deca_t_1_q1[0]),
    .Q2(counter_deca_t_1_q1[1]), .Q4(counter_deca_t_1_q1[2]), .Q8(counter_deca_t_1_q1[3]));
  not not_2 (not_2_out, counter_hexa_t_2_q1[2]);
  counter_hexa_t counter_hexa_t_2 (
    .Count(Start), .Clk(not_3_out), .Clear_prime(Reset_prime), .Q1(counter_hexa_t_2_q1[0]),
    .Q2(counter_hexa_t_2_q1[1]), .Q4(counter_hexa_t_2_q1[2]), .Q8(counter_hexa_t_2_q1[3]));
  not not_3 (not_3_out, counter_deca_t_2_q1[3]);
  counter_deca_t counter_deca_t_2 (
    .Count(Start), .Clk(clock_1_out), .Clear_prime(Reset_prime), .Q1(counter_deca_t_2_q1[0]),
    .Q2(counter_deca_t_2_q1[1]), .Q4(counter_deca_t_2_q1[2]), .Q8(counter_deca_t_2_q1[3]));
  Clock clock_1 (.out(clock_1_out));
  Hex_Digit_Display hex_digit_display_1 (.value(counter_hexa_t_1_q1));  // open: dp
  Hex_Digit_Display hex_digit_display_2 (.value(counter_hexa_t_2_q1));  // open: dp
  Hex_Digit_Display hex_digit_display_3 (.value(counter_deca_t_1_q1));  // open: dp
  Hex_Digit_Display hex_digit_display_4 (.value(counter_deca_t_2_q1));  // open: dp
endmodule
