// Logisim project counter.tpl.circ as structural Verilog: 3 circuits, main circuit d-flipflop
module d_flipflop (
  input  Clk,
  input  D,
  input  Rst_prime,
  output Q,
  output Q_prime
);

  wire nand_1_out, nand_2_out, nand_3_out, nand_4_out;

  nand nand_1 (nand_1_out, nand_4_out, nand_2_out);
  nand nand_2 (nand_2_out, nand_1_out, Clk, Rst_prime);
  nand nand_3 (nand_3_out, nand_2_out, Clk, nand_4_out);
  nand nand_4 (nand_4_out, nand_3_out, D, Rst_prime);
  nand nand_5 (Q, nand_2_out, Q_prime);
  nand nand_6 (Q_prime, Q, nand_3_out, Rst_prime);
endmodule

module jk_flipflop (
  input  J,
  input  K,
  input  Clk,
  input  Rst_prime,
  output Q,
  output Q_prime
);

  wire and_1_out, and_2_out, not_1_out, or_1_out;

  and and_1 (and_1_out, Q_prime, J);
  not not_1 (not_1_out, K);
  and and_2 (and_2_out, not_1_out, Q);
  or or_1 (or_1_out, and_1_out, and_2_out);
  d_flipflop d_flipflop_1 (.Clk(Clk), .D(or_1_out), .Rst_prime(Rst_prime), .Q(Q), .Q_prime(Q_prime));
endmodule

module t_flipflop (
  input  T,
  input  Clk,
  input  Rst_prime,
  output Q,
  output Q_prime
);

  wire xor_1_out;

  xor xor_1 (xor_1_out, T, Q);
  d_flipflop d_flipflop_1 (.Clk(Clk), .D(xor_1_out), .Rst_prime(Rst_prime), .Q(Q), .Q_prime(Q_prime));
endmodule
