# Fritzing sketch flipflop-d-clk (saved by Fritzing 0.9.3b)
breadboards: 1

parts:
  D = Pushbutton [package="[THT]"]
  R2 = Resistor [tolerance=±5% resistance=1k package=THT]
  Q = LED - 5mm [color="Red (633nm)" package="5 mm [THT]"]
  Q' = LED - 5mm [color="Red (633nm)" package="5 mm [THT]"]
  IC1 = 7400 [package="DIP (Dual Inline) [THT]"]
  IC2 = 7402 [package="DIP (Dual Inline) [THT]"]
  U1 = 555 Timer [package="DIP8 [THT]"]
  R3 = Resistor [tolerance=±5% resistance=1k package=THT]
  R4 = Resistor [tolerance=±5% resistance=10M package=THT]
  C1 = Ceramic Capacitor [capacitance=10nF package="100 mil [THT, multilayer]"]
  C2 = Tantalum Capacitor [capacitance=100nF package="100 mil [THT, tantalum]"]
  CLK = LED - 5mm [color="Yellow (585nm)" package="5 mm [THT]"]

nets:
  VCC: D.Pin_1, D.Pin_2, IC1.VCC, IC2.VCC, U1.Pin_8, R3.Pin_0
  N1: D.Pin_3, D.Pin_4, R2.Pin_0, IC2.4B
  GND: R2.Pin_1, Q.cathode, Q'.cathode, IC1.GND, IC2.GND, U1.Pin_1, C2.-, CLK.cathode
  N2: Q.anode, IC1.1Y, IC1.2A
  N3: Q'.anode, IC1.1B, IC1.2Y
  N4: IC1.1A, IC1.3A, IC1.4Y
  N5: IC1.2B, IC1.3Y
  N6: IC1.3B, IC1.4B, IC2.3A, IC2.4A, U1.Pin_3, CLK.anode
  N7: IC1.4A, IC2.1Y, IC2.2A
  N8: IC2.1A, IC2.3B, IC2.4Y
  N9: IC2.2B, IC2.3Y
  N10: U1.Pin_2, U1.Pin_6, R4.Pin_0, C2.+
  N11: U1.Pin_5, C1.1
  N12: U1.Pin_7, R3.Pin_1, R4.Pin_1

notes:
  D Flip-Flop (Master-Slave Positive-Edge)

custom parts:
  7400: Quad 2-input NAND gate
  7402: Quad 2-input NOR gate
